# Fritzing sketch displays (saved by Fritzing 0.9.3b)

parts:
  Raspberry_Pi_1 = Raspberry Pi 3 [part_number=RPI-3-V1.2]
  U4 = Display [part_number=0532610819 package=Picoblade-53261-0819]  # not connected
  U5 = Display [part_number=0532610819 package=Picoblade-53261-0819]
  U6 = Display [part_number=0532610819 package=Picoblade-53261-0819]
  Raspberry_Pi_2 = Raspberry Pi 3 [part_number=RPI-3-V1.2]

nets:
  3V3: Raspberry_Pi_1.3v3, U5.3V3
  N1: Raspberry_Pi_1.GPIO10, U5.DIN
  N2: Raspberry_Pi_1.GPIO11, U5.CLK
  N3: Raspberry_Pi_1.GPIO21, U5.DC
  N4: Raspberry_Pi_1.GPIO16, U5.RST
  N5: Raspberry_Pi_1.GPIO7, U5.CS
  N6: Raspberry_Pi_1.GPIO23, U5.BUSY
  GND: Raspberry_Pi_1.GND, U5.GND
  N7: U6.BUSY, Raspberry_Pi_2.GPIO24
  N8: U6.RST, Raspberry_Pi_2.GPIO17
  N9: U6.DC, Raspberry_Pi_2.GPIO25
  N10: U6.CS, Raspberry_Pi_2.GPIO8
  N11: U6.CLK, Raspberry_Pi_2.GPIO11
  N12: U6.DIN, Raspberry_Pi_2.GPIO10
  GND_2: U6.GND, Raspberry_Pi_2.GND
  3V3_2: U6.3V3, Raspberry_Pi_2.3v3

notes:
  4.2inch e-Paper
  Display
  7.5 inch e-Paper
  Display

custom parts:
  Display: Molex Picoblade Header: 1.25mm Pitch Miniature Crimping Connector. Single Row Straight Pin Header (SMT)
